# Fritzing sketch Untitled Sketch 3 (saved by Fritzing 0.9.3b)
breadboards: 1

parts:
  Part1 = Arduino Uno (Rev3)
  R1 = Resistor [tolerance=±5% resistance=220 package=THT]
  Q1 = NPN-Transistor [package="TO92 [THT]"]
  D1 = Rectifier Diode [part_number=1N4001 package="300 mil [THT]"]
  M1 = DC Motor
  Part2 = Soil Moisture Sensor

nets:
  N1: Part1.D8, Part2.SIG
  N2: Part1.D13/SCK, R1.Pin_1
  5V: Part1.5V, D1.cathode, M1.pin_1, Part2.VCC
  GND: Part1.GND, Q1.E, Part2.GND
  N3: R1.Pin_0, Q1.B
  N4: Q1.C, D1.anode, M1.pin_2

// code stored in the sketch: Untitled3.ino
int WATERPUMP = 13; //motor pump connected to pin 13
int sensor = 8; //sensor digital pin vonnected to pin 8
int val; //This variable stores the value received from Soil moisture sensor.

void setup() {
  
  pinMode(13,OUTPUT); //Set pin 13 as OUTPUT pin
  pinMode(8,INPUT); //Set pin 8 as input pin, to receive data from Soil moisture sensor.
  //Initialize serial and wait for port to open:
  Serial.begin(9600); // opens serial port, sets data rate to 9600 bps
  while (! Serial);// wait for serial port to connect. Needed for native USB
  Serial.println("Speed 0 to 255");
}

void loop()
  { 
  if (Serial.available()) //loop to operate motor
  {
    int speed = Serial.parseInt(); // to read the number entered as text in the Serial Monitor 
    if (speed >= 0 && speed <= 255)
    {
      analogWrite(WATERPUMP, speed);// tuns on the motor at specified speed 
    }
  }
  val = digitalRead(8);  //Read data from soil moisture sensor  
  if(val == LOW) 
  {
  digitalWrite(13,LOW); //if soil moisture sensor provides LOW value send LOW value to motor pump and motor pump goes off
  }
  else
  {
  digitalWrite(13,HIGH); //if soil moisture sensor provides HIGH value send HIGH value to motor pump and motor pump get on
  }
  delay(400); //Wait for few second and then continue the loop.
}
